// Logisim project Portas Lógicas (Gates) - Simu.circ as structural Verilog: 1 circuit, main circuit main
module main (
  input  A,
  input  A_2,
  input  C,
  input  B,
  input  B_2,
  input  A_3,
  input  A_4,
  input  B_3,
  input  B_4,
  input  A_5,
  input  C_2,
  input  D,
  input  A_6,
  input  B_5,
  input  A_7,
  input  B_6,
  input  A_8,
  input  B_7
);

  wire and_1_out, and_2_out, and_3_out, and_4_out, nand_1_out, nor_1_out, not_1_out, or_1_out, or_2_out,
       xor_1_out;

  and and_1 (and_1_out, A_2, B);
  or or_1 (or_1_out, A_3, B_3, B_3, B_3);
  not not_1 (not_1_out, A_5);
  nand nand_1 (nand_1_out, A_6, B_5);
  nor nor_1 (nor_1_out, A_7, B_6);
  xor xor_1 (xor_1_out, A_8, B_7);
  LED led_1 (.in(and_1_out));
  LED led_2 (.in(or_1_out));
  LED led_3 (.in(not_1_out));
  LED led_4 (.in(nand_1_out));
  LED led_5 (.in(nor_1_out));
  LED led_6 (.in(xor_1_out));
  and and_2 (and_2_out, A, C, B_2);
  and and_3 (and_3_out, A_4, B_4);
  or or_2 (or_2_out, C_2, D);
  LED led_7 (.in(and_2_out));
  and and_4 (and_4_out, and_3_out, or_2_out);
  LED led_8 (.in(and_4_out));

  // Notes on the sheet:
  //   X
  //   X
  //   X
  //   X
  //   X
  //   X
  //   S
  //   S
endmodule
