// Logisim project Atividade 2 - q04.circ as structural Verilog: 1 circuit, main circuit main
module main (
  input  A,
  input  B,
  input  C,
  input  D,
  input  E
);

  wire and_1_out, or_1_out, or_2_out;

  or or_1 (or_1_out, A, B, C);
  or or_2 (or_2_out, D, E);
  and and_1 (and_1_out, or_1_out, or_2_out);
  LED led_1 (.in(and_1_out));

  // Notes on the sheet:
  //   S
  //   S=(A+!B+A) * (D*!E)
endmodule
