// Logisim project Atividade 2 - q05.circ as structural Verilog: 1 circuit, main circuit main
module main (
  input  A,
  input  B,
  input  D,
  input  C,
  input  E,
  input  F
);

  wire and_1_out, and_2_out, or_1_out, or_2_out;

  or or_1 (or_1_out, B, D);
  and and_1 (and_1_out, E, F);
  and and_2 (and_2_out, A, A, or_1_out);
  or or_2 (or_2_out, and_2_out, C, and_1_out);
  LED led_1 (.in(or_2_out));

  // Notes on the sheet:
  //   S1
  //   S3
  //   S2
  //   S
endmodule
