// Logisim project Atividade 2 - q06.circ as structural Verilog: 1 circuit, main circuit main
module main (
  input  A,
  input  B,
  input  C,
  input  D,
  input  A_2,
  input  B_2,
  input  C_2,
  input  D_2,
  input  A_3,
  input  B_3,
  input  C_3,
  input  D_3,
  input  A_4,
  input  B_4,
  input  C_4,
  input  D_4
);

  wire and_1_out, and_2_out, and_3_out, and_4_out, not_1_out, not_2_out, not_3_out, not_4_out, not_5_out,
       not_6_out, not_7_out, not_8_out, or_1_out;

  not not_1 (not_1_out, A);
  not not_2 (not_2_out, B);
  not not_3 (not_3_out, C);
  not not_4 (not_4_out, A_2);
  not not_5 (not_5_out, B_2);
  not not_6 (not_6_out, B_3);
  not not_7 (not_7_out, C_3);
  not not_8 (not_8_out, D_3);
  and and_1 (and_1_out, not_1_out, not_2_out, not_3_out, D);
  and and_2 (and_2_out, not_4_out, not_5_out, C_2, D_2);
  and and_3 (and_3_out, A_3, not_6_out, not_7_out, not_8_out);
  and and_4 (and_4_out, A_4, B_4, C_4, D_4);
  or or_1 (or_1_out, and_1_out, and_2_out, and_3_out, and_4_out);
  LED led_1 (.in(or_1_out));

  // Notes on the sheet:
  //   S
  //   S=(A*B*C*!D) + (!A*B*C*D) + (!A*!B*!C*!D)
endmodule
